# Fritzing sketch cyberhiveSchematic (saved by Fritzing 0.8.5b)
breadboards: 1

parts:
  Part1 = Arduino Uno (Rev3)
  Momentary_Toggle = Momentary Switch [package=tactile-pth]
  DHT22_01 = DHT22 Humidity and Temperature Sensor
  DHT22_02 = DHT22 Humidity and Temperature Sensor
  DHT22_03 = DHT22 Humidity and Temperature Sensor
  9_Volt_Power = Battery block 9V
  7SEG_Temp = 7-Segment LED I2C Backpack (white)
  7SEG_humidity = 7-Segment LED I2C Backpack (red)
  LED1 = LEDs [package=led-0603]
  LED2 = LEDs [package=led-0603]
  LED3 = LEDs [package=led-0603]
  led_current_limiter = Resistor [tolerance=±5% resistance=1k package=THT]

nets:
  N1: Part1.D8, LED3.A
  N2: Part1.D9_PWM, Momentary_Toggle.3
  N3: Part1.A4/SDA, 7SEG_Temp.SDA, 7SEG_humidity.SDA
  N4: Part1.A5/SCL, 7SEG_Temp.SCL, 7SEG_humidity.SCL
  N5: Part1.D3_PWM, DHT22_01.DATA
  N6: Part1.D4, DHT22_02.DATA
  N7: Part1.D5_PWM, DHT22_03.DATA
  N8: Part1.D6_PWM, LED1.A
  N9: Part1.D7, LED2.A
  VDD: Part1.5V, DHT22_01.VDD, DHT22_02.VDD, DHT22_03.VDD, 7SEG_Temp.V+, 7SEG_humidity.V+
  GND: Part1.GND, Momentary_Toggle.1, DHT22_01.GND, DHT22_02.GND, DHT22_03.GND, 9_Volt_Power.-, 7SEG_Temp.GND, 7SEG_humidity.GND, led_current_limiter.Pin_1
  N10: Part1.VIN, 9_Volt_Power.+
  N11: LED1.C, LED2.C
  N12: LED3.C, led_current_limiter.Pin_0

custom parts:
  7-Segment LED I2C Backpack (white): 4-digit, 7-segment LED Display with I2C Control
  7-Segment LED I2C Backpack (red): 4-digit, 7-segment LED Display with I2C Control
